# Fritzing sketch lightning_camera_trigger (saved by Fritzing 0.9.0b)
breadboards: 1

parts:
  Arduino = Arduino Uno (Rev3)
  R1 = Resistor [tolerance=±5% resistance=100k package=THT]
  R2 = Photocell (LDR) [package=THT]
  R3 = Resistor [tolerance=±5% resistance=220 package=THT]
  LED1 = LED - 5mm [color="Infrared (940nm)" package="5 mm [THT]"]
  LED2 = LED - 5mm [color="Yellow (595nm)" package="5 mm [THT]"]

nets:
  N1: Arduino.A0, R1.Pin_1, R2.pin_0
  N2: Arduino.D13/SCK, LED2.anode
  N3: Arduino.GND, R1.Pin_0, R3.Pin_0
  N4: Arduino.5V, R2.pin_1
  N5: R3.Pin_1, LED1.cathode
  N6: LED1.anode, LED2.cathode
